// Logisim project CS382_CPU.circ as structural Verilog: 16 circuits, main circuit main
module main (
);

  wire alu_1_z, ALUSrc, Branch, ClockTunnel, MemRead, MemToReg, MemWrite, RegDst, RegWrite;
  wire [1:0] ALUop;
  wire [3:0] alucontrol_1_action;
  wire [4:0] rs, rt, t, topmux_1_readreg2;
  wire [5:0] funct, i_1_opcode;
  wire [15:0] shifter_1_out;
  wire [15:6] IMM;
  wire [31:0] address_1_i;
  wire [63:0] addforpc_1_next_pc, addmid_1_brpc, alu_1_aluout, ALUout, datamemory_1_readdatam, leftmux_1_pc,
       midmux_1_inputb, pc_1_pcoutput, RegData2, RegDataW, registerfile_1_regdata1;

  ADDFORPC addforpc_1 (.PC_input_to_adder(pc_1_pcoutput), .Next_PC(addforpc_1_next_pc));
  Shifter #(.width(16)) shifter_1 (.in({IMM, funct}), .\dist (4'b0010), .out(shifter_1_out));
  Control control_1 (
    .opcode(i_1_opcode), .RegDst(RegDst), .ALUSrc(ALUSrc), .MemtoReg(MemToReg), .RegWrite(RegWrite),
    .MemRead(MemRead), .MemWrite(MemWrite), .Branch(Branch), .ALUop(ALUop));
  ADDmid addmid_1 (.I(shifter_1_out), .PCInputAdder(addforpc_1_next_pc), .BRPC(addmid_1_brpc));
  PC pc_1 (.Clock(ClockTunnel), .MUXtoPC(leftmux_1_pc), .PCOutput(pc_1_pcoutput));
  LeftMUX leftmux_1 (.PBR(alu_1_z), .ALUout(addmid_1_brpc), .nextPC(addforpc_1_next_pc), .PC(leftmux_1_pc));
  Clock clock_1 (.out(ClockTunnel));
  I i_1 (
    .Iinput(address_1_i), .opcode(i_1_opcode), .funct(funct), .shamt(IMM[10:6]), .rd(IMM[15:11]), .t(t),
    .rt(rt), .rs(rs));
  TopMUX topmux_1 (.Reg2Loc(RegDst), .T(IMM[15:11]), .M(rt), .ReadReg2(topmux_1_readreg2));
  RegisterFile registerfile_1 (
    .RegWrite(RegWrite), .Clock(ClockTunnel), .WriteReg(topmux_1_readreg2), .RegDataW(RegDataW),
    .ReadReg2(rt), .ReadReg1(rs), .RegData1(registerfile_1_regdata1), .RegData2(RegData2));
  ALU alu_1 (
    .A(registerfile_1_regdata1), .B(midmux_1_inputb), .Action(alucontrol_1_action), .Z(alu_1_z),
    .ALUOut(alu_1_aluout));
  Address address_1 (.Clock(ClockTunnel), .PCOutput(pc_1_pcoutput), .I(address_1_i));
  ALUControl alucontrol_1 (.funct(funct), .ALUop(ALUop), .Action(alucontrol_1_action));
  BottomMUX bottommux_1 (
    .MemToReg(MemToReg), .ReadDataM(datamemory_1_readdatam), .ALUout(ALUout), .nextpc(addforpc_1_next_pc),
    .LinkReg(ClockTunnel), .ToRegDataW(RegDataW));
  DataMemory datamemory_1 (
    .Address(alu_1_aluout), .WriteDataM(RegData2), .MemWrite(MemWrite), .Clock(ClockTunnel),
    .MemRead(MemRead), .ReadDataM(datamemory_1_readdatam));
  MidMUX midmux_1 (.IMM({IMM, funct}), .RegData2(RegData2), .ALUsrc(ALUSrc), .InputB(midmux_1_inputb));

  // Other names for the same wires on the sheet: IMM[5:0] = funct; rd[4:0] = IMM[15:11]; LinkReg = ClockTunnel;
  //   s[4:0] = IMM[10:6]
endmodule

module PC (
  input  [63:0] MUXtoPC,
  input  Clock,
  output [63:0] PCOutput
);

  Register #(.width(64)) register_1 (.D(MUXtoPC), .clk(Clock), .Q(PCOutput));  // open: en, clr
endmodule

module ADDFORPC (
  input  [63:0] PC_input_to_adder,
  output [63:0] Next_PC
);

  Adder #(.width(64)) adder_1 (.a(64'h1), .b(PC_input_to_adder), .out(Next_PC));  // open: cin, cout
endmodule

module BottomMUX (
  input  [63:0] ALUout,
  input  [63:0] ReadDataM,
  input  [63:0] nextpc,
  input  LinkReg,
  input  MemToReg,
  output [63:0] ToRegDataW
);

  wire [63:0] multiplexer_1_out;

  Multiplexer #(.width(64)) multiplexer_1 (.in0(ALUout), .in1(ReadDataM), .out(multiplexer_1_out), .sel(MemToReg));
  Multiplexer #(.width(64)) multiplexer_2 (.in0(multiplexer_1_out), .in1(nextpc), .out(ToRegDataW), .sel(LinkReg));
endmodule

module LeftMUX (
  input  [63:0] nextPC,
  input  [63:0] ALUout,
  input  PBR,
  output [63:0] PC
);

  Multiplexer #(.width(64)) multiplexer_1 (.in0(nextPC), .in1(ALUout), .out(PC), .sel(PBR));
endmodule

module ADDmid (
  input  [15:0] I,
  input  [63:0] PCInputAdder,
  output [63:0] BRPC
);

  wire [63:0] bit_extender_1_out;

  assign bit_extender_1_out = {{48{I[15]}}, I};  // Bit_Extender bit_extender_1
  Adder #(.width(64)) adder_1 (.a(bit_extender_1_out), .b(PCInputAdder), .out(BRPC));  // open: cin, cout
endmodule

module TopMUX (
  input  [4:0] T,
  input  [4:0] M,
  input  Reg2Loc,
  output [4:0] ReadReg2
);

  Multiplexer #(.width(5)) multiplexer_1 (.in0(T), .in1(M), .out(ReadReg2), .sel(Reg2Loc));
endmodule

module MidMUX (
  input  [63:0] RegData2,
  input  [15:0] IMM,
  input  ALUsrc,
  output [63:0] InputB
);

  wire [63:0] bit_extender_1_out;

  assign bit_extender_1_out = {{48{IMM[15]}}, IMM};  // Bit_Extender bit_extender_1
  Multiplexer #(.width(64)) multiplexer_1 (.in0(RegData2), .in1(bit_extender_1_out), .out(InputB), .sel(ALUsrc));
endmodule

module Address (
  input  [63:0] PCOutput,
  input  Clock,
  output [31:0] I
);

  wire [23:0] bit_extender_1_out;

  Bit_Extender #(.in_width(64), .out_width(24)) bit_extender_1 (.in(PCOutput), .out(bit_extender_1_out));
  RAM #(.addrWidth(24), .dataWidth(32), .enables("line")) ram_1 (
    .addr(bit_extender_1_out), .we(1'b0), .clk(Clock), .dout(I));  // open: din
endmodule

module RegisterFile (
  input  Clock,
  input  [4:0] ReadReg1,
  input  [4:0] WriteReg,
  input  [63:0] RegDataW,
  input  RegWrite,
  input  [4:0] ReadReg2,
  output [63:0] RegData1,
  output [63:0] RegData2
);

  wire and_1_out, and_2_out, and_3_out, and_4_out, and_5_out, and_6_out, and_7_out, and_8_out, and_9_out,
       and_10_out, and_11_out, and_12_out, and_13_out, and_14_out, and_15_out, and_16_out, and_17_out,
       and_18_out, and_19_out, and_20_out, and_21_out, and_22_out, and_23_out, and_24_out, and_25_out,
       and_26_out, and_27_out, and_28_out, and_29_out, and_30_out, and_31_out, and_32_out, decoder_1_out0,
       decoder_1_out1, decoder_1_out2, decoder_1_out3, decoder_1_out4, decoder_1_out5, decoder_1_out6,
       decoder_1_out7, decoder_1_out8, decoder_1_out9, decoder_1_out10, decoder_1_out11, decoder_1_out12,
       decoder_1_out13, decoder_1_out14, decoder_1_out15, decoder_1_out16, decoder_1_out17, decoder_1_out18,
       decoder_1_out19, decoder_1_out20, decoder_1_out21, decoder_1_out22, decoder_1_out23, decoder_1_out24,
       decoder_1_out25, decoder_1_out26, decoder_1_out27, decoder_1_out28, decoder_1_out29, decoder_1_out30,
       decoder_1_out31;
  wire [63:0] X0_q, X1_q, X2_q, X3_q, X4_q, X5_q, X6_q, X7_q, X8_q, X9_q, X10_q, X11_q, X12_q, X13_q, X14_q,
       X15_q, X16_q, X17_q, X18_q, X19_q, X20_q, X21_q, X22_q, X23_q, X24_q, X25_q, X26_q, X27_q, X28_q,
       X29_q, X30_q, X31_q;

  Decoder #(.enable("false"), .select(5)) decoder_1 (
    .out0(decoder_1_out0), .out1(decoder_1_out1), .out2(decoder_1_out2), .out3(decoder_1_out3),
    .out4(decoder_1_out4), .out5(decoder_1_out5), .out6(decoder_1_out6), .out7(decoder_1_out7),
    .out8(decoder_1_out8), .out9(decoder_1_out9), .out10(decoder_1_out10), .out11(decoder_1_out11),
    .out12(decoder_1_out12), .out13(decoder_1_out13), .out14(decoder_1_out14), .out15(decoder_1_out15),
    .out16(decoder_1_out16), .out17(decoder_1_out17), .out18(decoder_1_out18), .out19(decoder_1_out19),
    .out20(decoder_1_out20), .out21(decoder_1_out21), .out22(decoder_1_out22), .out23(decoder_1_out23),
    .out24(decoder_1_out24), .out25(decoder_1_out25), .out26(decoder_1_out26), .out27(decoder_1_out27),
    .out28(decoder_1_out28), .out29(decoder_1_out29), .out30(decoder_1_out30), .out31(decoder_1_out31),
    .sel(WriteReg));
  and and_1 (and_1_out, RegWrite, decoder_1_out0);
  and and_2 (and_2_out, RegWrite, decoder_1_out1);
  and and_3 (and_3_out, RegWrite, decoder_1_out2);
  and and_4 (and_4_out, RegWrite, decoder_1_out3);
  and and_5 (and_5_out, RegWrite, decoder_1_out4);
  and and_6 (and_6_out, RegWrite, decoder_1_out5);
  and and_7 (and_7_out, RegWrite, decoder_1_out6);
  and and_8 (and_8_out, RegWrite, decoder_1_out7);
  and and_9 (and_9_out, RegWrite, decoder_1_out8);
  and and_10 (and_10_out, RegWrite, decoder_1_out9);
  and and_11 (and_11_out, RegWrite, decoder_1_out10);
  and and_12 (and_12_out, RegWrite, decoder_1_out11);
  and and_13 (and_13_out, RegWrite, decoder_1_out12);
  and and_14 (and_14_out, RegWrite, decoder_1_out13);
  and and_15 (and_15_out, RegWrite, decoder_1_out14);
  and and_16 (and_16_out, RegWrite, decoder_1_out15);
  and and_17 (and_17_out, RegWrite, decoder_1_out16);
  and and_18 (and_18_out, RegWrite, decoder_1_out17);
  and and_19 (and_19_out, RegWrite, decoder_1_out18);
  and and_20 (and_20_out, RegWrite, decoder_1_out19);
  and and_21 (and_21_out, RegWrite, decoder_1_out20);
  and and_22 (and_22_out, RegWrite, decoder_1_out21);
  and and_23 (and_23_out, RegWrite, decoder_1_out22);
  and and_24 (and_24_out, RegWrite, decoder_1_out23);
  and and_25 (and_25_out, RegWrite, decoder_1_out24);
  and and_26 (and_26_out, RegWrite, decoder_1_out25);
  and and_27 (and_27_out, RegWrite, decoder_1_out26);
  and and_28 (and_28_out, RegWrite, decoder_1_out27);
  and and_29 (and_29_out, RegWrite, decoder_1_out28);
  and and_30 (and_30_out, RegWrite, decoder_1_out29);
  and and_31 (and_31_out, RegWrite, decoder_1_out30);
  and and_32 (and_32_out, RegWrite, decoder_1_out31);
  Register #(.width(64)) X0 (.D(RegDataW), .en(and_1_out), .clk(Clock), .Q(X0_q));  // open: clr
  Register #(.width(64)) X1 (.D(RegDataW), .en(and_2_out), .clk(Clock), .Q(X1_q));  // open: clr
  Register #(.width(64)) X2 (.D(RegDataW), .en(and_3_out), .clk(Clock), .Q(X2_q));  // open: clr
  Register #(.width(64)) X3 (.D(RegDataW), .en(and_4_out), .clk(Clock), .Q(X3_q));  // open: clr
  Register #(.width(64)) X4 (.D(RegDataW), .en(and_5_out), .clk(Clock), .Q(X4_q));  // open: clr
  Register #(.width(64)) X5 (.D(RegDataW), .en(and_6_out), .clk(Clock), .Q(X5_q));  // open: clr
  Register #(.width(64)) X6 (.D(RegDataW), .en(and_7_out), .clk(Clock), .Q(X6_q));  // open: clr
  Register #(.width(64)) X7 (.D(RegDataW), .en(and_8_out), .clk(Clock), .Q(X7_q));  // open: clr
  Register #(.width(64)) X8 (.D(RegDataW), .en(and_9_out), .clk(Clock), .Q(X8_q));  // open: clr
  Register #(.width(64)) X9 (.D(RegDataW), .en(and_10_out), .clk(Clock), .Q(X9_q));  // open: clr
  Register #(.width(64)) X10 (.D(RegDataW), .en(and_11_out), .clk(Clock), .Q(X10_q));  // open: clr
  Register #(.width(64)) X11 (.D(RegDataW), .en(and_12_out), .clk(Clock), .Q(X11_q));  // open: clr
  Register #(.width(64)) X12 (.D(RegDataW), .en(and_13_out), .clk(Clock), .Q(X12_q));  // open: clr
  Register #(.width(64)) X13 (.D(RegDataW), .en(and_14_out), .clk(Clock), .Q(X13_q));  // open: clr
  Register #(.width(64)) X14 (.D(RegDataW), .en(and_15_out), .clk(Clock), .Q(X14_q));  // open: clr
  Register #(.width(64)) X15 (.D(RegDataW), .en(and_16_out), .clk(Clock), .Q(X15_q));  // open: clr
  Register #(.width(64)) X16 (.D(RegDataW), .en(and_17_out), .clk(Clock), .Q(X16_q));  // open: clr
  Register #(.width(64)) X17 (.D(RegDataW), .en(and_18_out), .clk(Clock), .Q(X17_q));  // open: clr
  Register #(.width(64)) X18 (.D(RegDataW), .en(and_19_out), .clk(Clock), .Q(X18_q));  // open: clr
  Register #(.width(64)) X19 (.D(RegDataW), .en(and_20_out), .clk(Clock), .Q(X19_q));  // open: clr
  Register #(.width(64)) X20 (.D(RegDataW), .en(and_21_out), .clk(Clock), .Q(X20_q));  // open: clr
  Register #(.width(64)) X21 (.D(RegDataW), .en(and_22_out), .clk(Clock), .Q(X21_q));  // open: clr
  Register #(.width(64)) X22 (.D(RegDataW), .en(and_23_out), .clk(Clock), .Q(X22_q));  // open: clr
  Register #(.width(64)) X23 (.D(RegDataW), .en(and_24_out), .clk(Clock), .Q(X23_q));  // open: clr
  Register #(.width(64)) X24 (.D(RegDataW), .en(and_25_out), .clk(Clock), .Q(X24_q));  // open: clr
  Register #(.width(64)) X25 (.D(RegDataW), .en(and_26_out), .clk(Clock), .Q(X25_q));  // open: clr
  Register #(.width(64)) X26 (.D(RegDataW), .en(and_27_out), .clk(Clock), .Q(X26_q));  // open: clr
  Register #(.width(64)) X27 (.D(RegDataW), .en(and_28_out), .clk(Clock), .Q(X27_q));  // open: clr
  Register #(.width(64)) X28 (.D(RegDataW), .en(and_29_out), .clk(Clock), .Q(X28_q));  // open: clr
  Register #(.width(64)) X29 (.D(RegDataW), .en(and_30_out), .clk(Clock), .Q(X29_q));  // open: clr
  Register #(.width(64)) X30 (.D(RegDataW), .en(and_31_out), .clk(Clock), .Q(X30_q));  // open: clr
  Register #(.width(64)) X31 (.D(RegDataW), .en(and_32_out), .clk(Clock), .Q(X31_q));  // open: clr
  Multiplexer #(.select(5), .width(64)) multiplexer_1 (
    .in0(X0_q), .in1(X1_q), .in2(X2_q), .in3(X3_q), .in4(X4_q), .in5(X5_q), .in6(X6_q), .in7(X7_q),
    .in8(X8_q), .in9(X9_q), .in10(X10_q), .in11(X11_q), .in12(X12_q), .in13(X13_q), .in14(X14_q),
    .in15(X15_q), .in16(X16_q), .in17(X17_q), .in18(X18_q), .in19(X19_q), .in20(X20_q), .in21(X21_q),
    .in22(X22_q), .in23(X23_q), .in24(X24_q), .in25(X25_q), .in26(X26_q), .in27(X27_q), .in28(X28_q),
    .in29(X29_q), .in30(X30_q), .in31(X31_q), .out(RegData1), .sel(ReadReg1));
  Multiplexer #(.select(5), .width(64)) multiplexer_2 (
    .in0(X0_q), .in1(X1_q), .in2(X2_q), .in3(X3_q), .in4(X4_q), .in5(X5_q), .in6(X6_q), .in7(X7_q),
    .in8(X8_q), .in9(X9_q), .in10(X10_q), .in11(X11_q), .in12(X12_q), .in13(X13_q), .in14(X14_q),
    .in15(X15_q), .in16(X16_q), .in17(X17_q), .in18(X18_q), .in19(X19_q), .in20(X20_q), .in21(X21_q),
    .in22(X22_q), .in23(X23_q), .in24(X24_q), .in25(X25_q), .in26(X26_q), .in27(X27_q), .in28(X28_q),
    .in29(X29_q), .in30(X30_q), .in31(X31_q), .out(RegData2), .sel(ReadReg2));

  // Other names for the same wires on the sheet: C = Clock; RegDataWT[63:0] = RegDataW; RegWriteT = RegWrite
endmodule

module I (
  input  [31:0] Iinput,
  output [5:0] funct,
  output [4:0] shamt,
  output [4:0] rd,
  output [4:0] t,
  output [4:0] rt,
  output [4:0] rs,
  output [5:0] opcode
);


  assign funct = Iinput[5:0];
  assign opcode = Iinput[31:26];
  assign rd = Iinput[15:11];
  assign rs = Iinput[25:21];
  assign rt = Iinput[20:16];
  assign shamt = Iinput[10:6];
  assign t = Iinput[20:16];
endmodule

module ALUControl (
  input  [1:0] ALUop,
  input  [5:0] funct,
  output [3:0] Action
);

  wire and_1_out, not_1_out, not_2_out, or_1_out;

  or or_1 (or_1_out, funct[3], funct[0]);
  and and_1 (and_1_out, ALUop[1], funct[1]);
  and and_2 (Action[0], ALUop[1], or_1_out);
  not not_1 (not_1_out, ALUop[1]);
  not not_2 (not_2_out, funct[2]);
  or or_2 (Action[2], ALUop[0], and_1_out);
  or or_3 (Action[1], not_1_out, not_2_out);

  assign Action[3] = 1'b0;
endmodule

module ALU (
  input  [3:0] Action,
  input  [63:0] A,
  input  [63:0] B,
  output Z,
  output [63:0] ALUOut
);
endmodule

module DataMemory (
  input  [63:0] Address,
  input  MemRead,
  input  MemWrite,
  input  Clock,
  input  [63:0] WriteDataM,
  output [63:0] ReadDataM
);

  wire [23:0] bit_extender_1_out;

  Bit_Extender #(.in_width(64), .out_width(24)) bit_extender_1 (.in(Address), .out(bit_extender_1_out));
  RAM #(.addrWidth(24), .dataWidth(64), .enables("line")) ram_1 (
    .addr(bit_extender_1_out), .we(MemRead), .oe(MemWrite), .clk(Clock), .din(WriteDataM), .dout(ReadDataM));
endmodule

module Control (
  input  [5:0] opcode,
  output RegDst,
  output ALUSrc,
  output MemtoReg,
  output RegWrite,
  output MemRead,
  output MemWrite,
  output Branch,
  output [1:0] ALUop
);

  wire not_1_out, not_2_out, not_3_out, not_4_out, not_5_out, not_6_out, not_7_out, not_8_out, not_9_out,
       not_10_out, not_11_out, not_12_out, not_13_out, not_14_out, not_15_out, not_16_out;

  not not_1 (not_1_out, opcode[5]);
  not not_2 (not_2_out, opcode[4]);
  not not_3 (not_3_out, opcode[3]);
  not not_4 (not_4_out, opcode[2]);
  not not_5 (not_5_out, opcode[1]);
  not not_6 (not_6_out, opcode[0]);
  and and_1 (ALUop[1], not_1_out, not_2_out, not_3_out, not_4_out, not_5_out, not_6_out);
  not not_7 (not_7_out, opcode[4]);
  not not_8 (not_8_out, opcode[3]);
  not not_9 (not_9_out, opcode[2]);
  and and_2 (MemRead, opcode[5], not_7_out, not_8_out, not_9_out, opcode[1], opcode[0]);
  not not_10 (not_10_out, opcode[4]);
  not not_11 (not_11_out, opcode[2]);
  and and_3 (MemWrite, opcode[5], not_10_out, opcode[3], not_11_out, opcode[1], opcode[0]);
  not not_12 (not_12_out, opcode[5]);
  not not_13 (not_13_out, opcode[4]);
  not not_14 (not_14_out, opcode[3]);
  not not_15 (not_15_out, opcode[1]);
  not not_16 (not_16_out, opcode[0]);
  and and_4 (ALUop[0], not_12_out, not_13_out, not_14_out, opcode[2], not_15_out, not_16_out);
  or or_1 (ALUSrc, MemRead, MemWrite);
  or or_2 (RegWrite, ALUop[1], MemRead);

  assign Branch = ALUop[0];
  assign MemtoReg = MemRead;
  assign RegDst = ALUop[1];

  // Notes on the sheet:
  //   For ALUop 0 is add, 1 is multiply
endmodule

module AndOrGate (
  input  CBR,
  input  Z,
  input  UBR,
  output BR
);

  wire and_1_out;

  and and_1 (and_1_out, CBR, Z);
  or or_1 (BR, and_1_out, UBR);
endmodule
