// Logisim project Fried_Liver.circ as structural Verilog: 16 circuits, main circuit main
module main (
);

  wire alu_1_z, alucontrol_1_action, ALUop, andorgate_1_br, ClockTunnel, control_1_alusrc, control_1_cbr,
       control_1_memread, control_1_memwrite, control_1_pbr, control_1_reg2loc, control_1_regwrite,
       control_1_ubr, LinkReg, MemToReg;
  wire [4:0] i_1_d, i_1_m, i_1_n, i_1_t, topmux_1_readreg2;
  wire [10:0] i_1_imm, i_1_immtoadd, i_1_opcode, i_1_opcodetoaluctrl;
  wire [31:0] address_1_i;
  wire [63:0] addforpc_1_next_pc, addmid_1_brpc, ALUout, bottommux_1_toregdataw, datamemory_1_readdatam,
       leftmux_1_pc, midmux_1_inputb, pc_1_pcoutput, RegData2, registerfile_1_regdata1;

  ADDFORPC addforpc_1 (.PC_input_to_adder(pc_1_pcoutput), .Next_PC(addforpc_1_next_pc));
  ADDmid addmid_1 (.I(i_1_immtoadd), .PCInputAdder(pc_1_pcoutput), .BRPC(addmid_1_brpc));
  AndOrGate andorgate_1 (.CBR(control_1_cbr), .Z(alu_1_z), .UBR(control_1_ubr), .BR(andorgate_1_br));
  PC pc_1 (.Clock(ClockTunnel), .MUXtoPC(leftmux_1_pc), .PCOutput(pc_1_pcoutput));
  LeftMUX leftmux_1 (
    .nextPC(addforpc_1_next_pc), .ALUout(ALUout), .PBR(control_1_pbr), .BR(andorgate_1_br),
    .BRPC(addmid_1_brpc), .PC(leftmux_1_pc));
  Clock clock_1 (.out(ClockTunnel));
  I i_1 (
    .Iinput(address_1_i), .opcode(i_1_opcode), .opcodeToALUctrl(i_1_opcodetoaluctrl), .D(i_1_d), .T(i_1_t),
    .N(i_1_n), .M(i_1_m), .immToAdd(i_1_immtoadd), .IMM(i_1_imm));
  Control control_1 (
    .I3121(i_1_opcode), .Reg2Loc(control_1_reg2loc), .ALUop(ALUop), .RegWrite(control_1_regwrite),
    .ALUsrc(control_1_alusrc), .MemRead(control_1_memread), .MemToReg(MemToReg),
    .MemWrite(control_1_memwrite), .LinkReg(LinkReg), .UBr(control_1_ubr), .CBr(control_1_cbr),
    .PBr(control_1_pbr));
  Address address_1 (.Clock(ClockTunnel), .PCOutput(pc_1_pcoutput), .I(address_1_i));
  TopMUX topmux_1 (.Reg2Loc(control_1_reg2loc), .T(i_1_t), .M(i_1_m), .ReadReg2(topmux_1_readreg2));
  RegisterFile registerfile_1 (
    .Clock(ClockTunnel), .WriteReg(i_1_d), .RegWrite(control_1_regwrite), .RegDataW(bottommux_1_toregdataw),
    .ReadReg2(topmux_1_readreg2), .ReadReg1(i_1_n), .RegData1(registerfile_1_regdata1), .RegData2(RegData2));
  ALU alu_1 (
    .Action(alucontrol_1_action), .A(registerfile_1_regdata1), .B(midmux_1_inputb), .ALUOut(ALUout),
    .Z(alu_1_z));
  DataMemory datamemory_1 (
    .MemRead(control_1_memread), .Address(ALUout), .WriteDataM(RegData2), .MemWrite(control_1_memwrite),
    .Clock(ClockTunnel), .ReadDataM(datamemory_1_readdatam));
  BottomMUX bottommux_1 (
    .MemToReg(MemToReg), .ReadDataM(datamemory_1_readdatam), .ALUout(ALUout), .nextpc(addforpc_1_next_pc),
    .LinkReg(LinkReg), .ToRegDataW(bottommux_1_toregdataw));
  MidMUX midmux_1 (.IMM(i_1_imm), .RegData2(RegData2), .ALUsrc(control_1_alusrc), .InputB(midmux_1_inputb));
  ALUControl alucontrol_1 (.I3121(i_1_opcodetoaluctrl), .ALUop(ALUop), .Action(alucontrol_1_action));

  // Notes on the sheet:
  //   CBR
  //   Reg2Loc
  //   RegWrite
  //   PBR
  //   MemWrite
  //   ALUsrc
  //   MemRead
  //   Kieran Corson and Ethan Shanahan
  //   I pledge my honor that I have abided by the Stevens Honor System.
endmodule

module PC (
  input  [63:0] MUXtoPC,
  input  Clock,
  output [63:0] PCOutput
);

  Register #(.width(64)) register_1 (.D(MUXtoPC), .clk(Clock), .Q(PCOutput));  // open: en, clr
endmodule

module ADDFORPC (
  input  [63:0] PC_input_to_adder,
  output [63:0] Next_PC
);

  Adder #(.width(64)) adder_1 (.a(64'h1), .b(PC_input_to_adder), .out(Next_PC));  // open: cin, cout
endmodule

module BottomMUX (
  input  [63:0] ALUout,
  input  [63:0] ReadDataM,
  input  [63:0] nextpc,
  input  LinkReg,
  input  MemToReg,
  output [63:0] ToRegDataW
);

  wire [63:0] multiplexer_1_out;

  Multiplexer #(.width(64)) multiplexer_1 (.in0(ALUout), .in1(ReadDataM), .out(multiplexer_1_out), .sel(MemToReg));
  Multiplexer #(.width(64)) multiplexer_2 (.in0(multiplexer_1_out), .in1(nextpc), .out(ToRegDataW), .sel(LinkReg));
endmodule

module LeftMUX (
  input  [63:0] nextPC,
  input  [63:0] ALUout,
  input  [63:0] BRPC,
  input  PBR,
  input  BR,
  output [63:0] PC
);

  wire [63:0] multiplexer_1_out;

  Multiplexer #(.width(64)) multiplexer_1 (.in0(nextPC), .in1(ALUout), .out(multiplexer_1_out), .sel(PBR));
  Multiplexer #(.width(64)) multiplexer_2 (.in0(multiplexer_1_out), .in1(BRPC), .out(PC), .sel(BR));
endmodule

module ADDmid (
  input  [10:0] I,
  input  [63:0] PCInputAdder,
  output [63:0] BRPC
);

  wire [63:0] bit_extender_1_out;

  assign bit_extender_1_out = {{53{I[10]}}, I};  // Bit_Extender bit_extender_1
  Adder #(.width(64)) adder_1 (.a(bit_extender_1_out), .b(PCInputAdder), .out(BRPC));  // open: cin, cout
endmodule

module TopMUX (
  input  [4:0] T,
  input  [4:0] M,
  input  Reg2Loc,
  output [4:0] ReadReg2
);

  Multiplexer #(.width(5)) multiplexer_1 (.in0(T), .in1(M), .out(ReadReg2), .sel(Reg2Loc));
endmodule

module MidMUX (
  input  [63:0] RegData2,
  input  [10:0] IMM,
  input  ALUsrc,
  output [63:0] InputB
);

  wire [63:0] bit_extender_1_out;

  assign bit_extender_1_out = {{53{IMM[10]}}, IMM};  // Bit_Extender bit_extender_1
  Multiplexer #(.width(64)) multiplexer_1 (.in0(RegData2), .in1(bit_extender_1_out), .out(InputB), .sel(ALUsrc));
endmodule

module Address (
  input  [63:0] PCOutput,
  input  Clock,
  output [31:0] I
);

  wire [23:0] bit_extender_1_out;

  Bit_Extender #(.in_width(64), .out_width(24)) bit_extender_1 (.in(PCOutput), .out(bit_extender_1_out));
  RAM #(.addrWidth(24), .dataWidth(32), .enables("line")) ram_1 (
    .addr(bit_extender_1_out), .we(1'b0), .clk(Clock), .dout(I));  // open: din
endmodule

module RegisterFile (
  input  Clock,
  input  [4:0] ReadReg1,
  input  [4:0] WriteReg,
  input  [63:0] RegDataW,
  input  RegWrite,
  input  [4:0] ReadReg2,
  output [63:0] RegData1,
  output [63:0] RegData2
);

  wire and_1_out, and_2_out, and_3_out, and_4_out, and_5_out, and_6_out, and_7_out, and_8_out, and_9_out,
       and_10_out, and_11_out, and_12_out, and_13_out, and_14_out, and_15_out, and_16_out, and_17_out,
       and_18_out, and_19_out, and_20_out, and_21_out, and_22_out, and_23_out, and_24_out, and_25_out,
       and_26_out, and_27_out, and_28_out, and_29_out, and_30_out, and_31_out, and_32_out, decoder_1_out0,
       decoder_1_out1, decoder_1_out2, decoder_1_out3, decoder_1_out4, decoder_1_out5, decoder_1_out6,
       decoder_1_out7, decoder_1_out8, decoder_1_out9, decoder_1_out10, decoder_1_out11, decoder_1_out12,
       decoder_1_out13, decoder_1_out14, decoder_1_out15, decoder_1_out16, decoder_1_out17, decoder_1_out18,
       decoder_1_out19, decoder_1_out20, decoder_1_out21, decoder_1_out22, decoder_1_out23, decoder_1_out24,
       decoder_1_out25, decoder_1_out26, decoder_1_out27, decoder_1_out28, decoder_1_out29, decoder_1_out30,
       decoder_1_out31;
  wire [63:0] X0_q, X1_q, X2_q, X3_q, X4_q, X5_q, X6_q, X7_q, X8_q, X9_q, X10_q, X11_q, X12_q, X13_q, X14_q,
       X15_q, X16_q, X17_q, X18_q, X19_q, X20_q, X21_q, X22_q, X23_q, X24_q, X25_q, X26_q, X27_q, X28_q,
       X29_q, X30_q, X31_q;

  Decoder #(.enable("false"), .select(5)) decoder_1 (
    .out0(decoder_1_out0), .out1(decoder_1_out1), .out2(decoder_1_out2), .out3(decoder_1_out3),
    .out4(decoder_1_out4), .out5(decoder_1_out5), .out6(decoder_1_out6), .out7(decoder_1_out7),
    .out8(decoder_1_out8), .out9(decoder_1_out9), .out10(decoder_1_out10), .out11(decoder_1_out11),
    .out12(decoder_1_out12), .out13(decoder_1_out13), .out14(decoder_1_out14), .out15(decoder_1_out15),
    .out16(decoder_1_out16), .out17(decoder_1_out17), .out18(decoder_1_out18), .out19(decoder_1_out19),
    .out20(decoder_1_out20), .out21(decoder_1_out21), .out22(decoder_1_out22), .out23(decoder_1_out23),
    .out24(decoder_1_out24), .out25(decoder_1_out25), .out26(decoder_1_out26), .out27(decoder_1_out27),
    .out28(decoder_1_out28), .out29(decoder_1_out29), .out30(decoder_1_out30), .out31(decoder_1_out31),
    .sel(WriteReg));
  and and_1 (and_1_out, RegWrite, decoder_1_out0);
  and and_2 (and_2_out, RegWrite, decoder_1_out1);
  and and_3 (and_3_out, RegWrite, decoder_1_out2);
  and and_4 (and_4_out, RegWrite, decoder_1_out3);
  and and_5 (and_5_out, RegWrite, decoder_1_out4);
  and and_6 (and_6_out, RegWrite, decoder_1_out5);
  and and_7 (and_7_out, RegWrite, decoder_1_out6);
  and and_8 (and_8_out, RegWrite, decoder_1_out7);
  and and_9 (and_9_out, RegWrite, decoder_1_out8);
  and and_10 (and_10_out, RegWrite, decoder_1_out9);
  and and_11 (and_11_out, RegWrite, decoder_1_out10);
  and and_12 (and_12_out, RegWrite, decoder_1_out11);
  and and_13 (and_13_out, RegWrite, decoder_1_out12);
  and and_14 (and_14_out, RegWrite, decoder_1_out13);
  and and_15 (and_15_out, RegWrite, decoder_1_out14);
  and and_16 (and_16_out, RegWrite, decoder_1_out15);
  and and_17 (and_17_out, RegWrite, decoder_1_out16);
  and and_18 (and_18_out, RegWrite, decoder_1_out17);
  and and_19 (and_19_out, RegWrite, decoder_1_out18);
  and and_20 (and_20_out, RegWrite, decoder_1_out19);
  and and_21 (and_21_out, RegWrite, decoder_1_out20);
  and and_22 (and_22_out, RegWrite, decoder_1_out21);
  and and_23 (and_23_out, RegWrite, decoder_1_out22);
  and and_24 (and_24_out, RegWrite, decoder_1_out23);
  and and_25 (and_25_out, RegWrite, decoder_1_out24);
  and and_26 (and_26_out, RegWrite, decoder_1_out25);
  and and_27 (and_27_out, RegWrite, decoder_1_out26);
  and and_28 (and_28_out, RegWrite, decoder_1_out27);
  and and_29 (and_29_out, RegWrite, decoder_1_out28);
  and and_30 (and_30_out, RegWrite, decoder_1_out29);
  and and_31 (and_31_out, RegWrite, decoder_1_out30);
  and and_32 (and_32_out, RegWrite, decoder_1_out31);
  Register #(.width(64)) X0 (.D(RegDataW), .en(and_1_out), .clk(Clock), .Q(X0_q));  // open: clr
  Register #(.width(64)) X1 (.D(RegDataW), .en(and_2_out), .clk(Clock), .Q(X1_q));  // open: clr
  Register #(.width(64)) X2 (.D(RegDataW), .en(and_3_out), .clk(Clock), .Q(X2_q));  // open: clr
  Register #(.width(64)) X3 (.D(RegDataW), .en(and_4_out), .clk(Clock), .Q(X3_q));  // open: clr
  Register #(.width(64)) X4 (.D(RegDataW), .en(and_5_out), .clk(Clock), .Q(X4_q));  // open: clr
  Register #(.width(64)) X5 (.D(RegDataW), .en(and_6_out), .clk(Clock), .Q(X5_q));  // open: clr
  Register #(.width(64)) X6 (.D(RegDataW), .en(and_7_out), .clk(Clock), .Q(X6_q));  // open: clr
  Register #(.width(64)) X7 (.D(RegDataW), .en(and_8_out), .clk(Clock), .Q(X7_q));  // open: clr
  Register #(.width(64)) X8 (.D(RegDataW), .en(and_9_out), .clk(Clock), .Q(X8_q));  // open: clr
  Register #(.width(64)) X9 (.D(RegDataW), .en(and_10_out), .clk(Clock), .Q(X9_q));  // open: clr
  Register #(.width(64)) X10 (.D(RegDataW), .en(and_11_out), .clk(Clock), .Q(X10_q));  // open: clr
  Register #(.width(64)) X11 (.D(RegDataW), .en(and_12_out), .clk(Clock), .Q(X11_q));  // open: clr
  Register #(.width(64)) X12 (.D(RegDataW), .en(and_13_out), .clk(Clock), .Q(X12_q));  // open: clr
  Register #(.width(64)) X13 (.D(RegDataW), .en(and_14_out), .clk(Clock), .Q(X13_q));  // open: clr
  Register #(.width(64)) X14 (.D(RegDataW), .en(and_15_out), .clk(Clock), .Q(X14_q));  // open: clr
  Register #(.width(64)) X15 (.D(RegDataW), .en(and_16_out), .clk(Clock), .Q(X15_q));  // open: clr
  Register #(.width(64)) X16 (.D(RegDataW), .en(and_17_out), .clk(Clock), .Q(X16_q));  // open: clr
  Register #(.width(64)) X17 (.D(RegDataW), .en(and_18_out), .clk(Clock), .Q(X17_q));  // open: clr
  Register #(.width(64)) X18 (.D(RegDataW), .en(and_19_out), .clk(Clock), .Q(X18_q));  // open: clr
  Register #(.width(64)) X19 (.D(RegDataW), .en(and_20_out), .clk(Clock), .Q(X19_q));  // open: clr
  Register #(.width(64)) X20 (.D(RegDataW), .en(and_21_out), .clk(Clock), .Q(X20_q));  // open: clr
  Register #(.width(64)) X21 (.D(RegDataW), .en(and_22_out), .clk(Clock), .Q(X21_q));  // open: clr
  Register #(.width(64)) X22 (.D(RegDataW), .en(and_23_out), .clk(Clock), .Q(X22_q));  // open: clr
  Register #(.width(64)) X23 (.D(RegDataW), .en(and_24_out), .clk(Clock), .Q(X23_q));  // open: clr
  Register #(.width(64)) X24 (.D(RegDataW), .en(and_25_out), .clk(Clock), .Q(X24_q));  // open: clr
  Register #(.width(64)) X25 (.D(RegDataW), .en(and_26_out), .clk(Clock), .Q(X25_q));  // open: clr
  Register #(.width(64)) X26 (.D(RegDataW), .en(and_27_out), .clk(Clock), .Q(X26_q));  // open: clr
  Register #(.width(64)) X27 (.D(RegDataW), .en(and_28_out), .clk(Clock), .Q(X27_q));  // open: clr
  Register #(.width(64)) X28 (.D(RegDataW), .en(and_29_out), .clk(Clock), .Q(X28_q));  // open: clr
  Register #(.width(64)) X29 (.D(RegDataW), .en(and_30_out), .clk(Clock), .Q(X29_q));  // open: clr
  Register #(.width(64)) X30 (.D(RegDataW), .en(and_31_out), .clk(Clock), .Q(X30_q));  // open: clr
  Register #(.width(64)) X31 (.D(RegDataW), .en(and_32_out), .clk(Clock), .Q(X31_q));  // open: clr
  Multiplexer #(.select(5), .width(64)) multiplexer_1 (
    .in0(X0_q), .in1(X1_q), .in2(X2_q), .in3(X3_q), .in4(X4_q), .in5(X5_q), .in6(X6_q), .in7(X7_q),
    .in8(X8_q), .in9(X9_q), .in10(X10_q), .in11(X11_q), .in12(X12_q), .in13(X13_q), .in14(X14_q),
    .in15(X15_q), .in16(X16_q), .in17(X17_q), .in18(X18_q), .in19(X19_q), .in20(X20_q), .in21(X21_q),
    .in22(X22_q), .in23(X23_q), .in24(X24_q), .in25(X25_q), .in26(X26_q), .in27(X27_q), .in28(X28_q),
    .in29(X29_q), .in30(X30_q), .in31(X31_q), .out(RegData1), .sel(ReadReg1));
  Multiplexer #(.select(5), .width(64)) multiplexer_2 (
    .in0(X0_q), .in1(X1_q), .in2(X2_q), .in3(X3_q), .in4(X4_q), .in5(X5_q), .in6(X6_q), .in7(X7_q),
    .in8(X8_q), .in9(X9_q), .in10(X10_q), .in11(X11_q), .in12(X12_q), .in13(X13_q), .in14(X14_q),
    .in15(X15_q), .in16(X16_q), .in17(X17_q), .in18(X18_q), .in19(X19_q), .in20(X20_q), .in21(X21_q),
    .in22(X22_q), .in23(X23_q), .in24(X24_q), .in25(X25_q), .in26(X26_q), .in27(X27_q), .in28(X28_q),
    .in29(X29_q), .in30(X30_q), .in31(X31_q), .out(RegData2), .sel(ReadReg2));

  // Other names for the same wires on the sheet: C = Clock; RegDataWT[63:0] = RegDataW; RegWriteT = RegWrite
endmodule

module I (
  input  [31:0] Iinput,
  output [4:0] T,
  output [4:0] D,
  output [4:0] N,
  output [10:0] immToAdd,
  output [10:0] IMM,
  output [4:0] M,
  output [10:0] opcode,
  output [10:0] opcodeToALUctrl
);


  assign D = Iinput[4:0];
  assign IMM = Iinput[20:10];
  assign immToAdd = Iinput[20:10];
  assign M = Iinput[20:16];
  assign N = Iinput[9:5];
  assign opcode = Iinput[31:21];
  assign opcodeToALUctrl = Iinput[31:21];
  assign T = Iinput[4:0];

  // Notes on the sheet:
  //   opcode for add is 00000000101
  //   ADD X2 x0 x1 = 00a20701
  //   ADD x2 x0 x1 = 00000000101 00010 00000 111000 00001
  //   MUL x2 x0 x1= 00000000111 00010 00000 111000 00001
endmodule

module ALUControl (
  input  [10:0] I3121,
  input  ALUop,
  output Action
);


  assign Action = ALUop;
endmodule

module ALU (
  input  [63:0] A,
  input  [63:0] B,
  input  Action,
  output Z,
  output [63:0] ALUOut
);

  wire [63:0] adder_1_out, multiplier_1_out;

  Adder #(.width(64)) adder_1 (.a(A), .b(B), .out(adder_1_out));  // open: cin, cout
  Multiplier #(.width(64)) multiplier_1 (.a(B), .b(A), .out(multiplier_1_out));  // open: cin, cout
  Multiplexer #(.width(64)) multiplexer_1 (.in0(adder_1_out), .in1(multiplier_1_out), .out(ALUOut), .sel(Action));
  Comparator #(.width(64)) comparator_1 (.a({64{1'b0}}), .b(ALUOut), .eq(Z));  // open: gt, lt
endmodule

module DataMemory (
  input  [63:0] Address,
  input  MemRead,
  input  MemWrite,
  input  Clock,
  input  [63:0] WriteDataM,
  output [63:0] ReadDataM
);

  wire [23:0] bit_extender_1_out;

  Bit_Extender #(.in_width(64), .out_width(24)) bit_extender_1 (.in(Address), .out(bit_extender_1_out));
  RAM #(.addrWidth(24), .dataWidth(64), .enables("line")) ram_1 (
    .addr(bit_extender_1_out), .we(MemWrite), .clk(Clock), .din(WriteDataM), .dout(ReadDataM));
endmodule

module Control (
  input  [10:0] I3121,
  output Reg2Loc,
  output ALUop,
  output RegWrite,
  output ALUsrc,
  output MemRead,
  output MemToReg,
  output MemWrite,
  output LinkReg,
  output UBr,
  output CBr,
  output PBr
);


  assign ALUop = I3121[1];
  assign ALUsrc = I3121[3];
  assign CBr = I3121[9];
  assign LinkReg = I3121[7];
  assign MemRead = I3121[4];
  assign MemToReg = I3121[5];
  assign MemWrite = I3121[6];
  assign PBr = I3121[10];
  assign Reg2Loc = I3121[0];
  assign RegWrite = I3121[2];
  assign UBr = I3121[8];

  // Notes on the sheet:
  //   For ALUop 0 is add, 1 is multiply
  //   opcode for reg reg add is 00000000101
  //   opcode for reg reg mul is 00000000111
  //   opcode for reg constant add 
endmodule

module AndOrGate (
  input  CBR,
  input  Z,
  input  UBR,
  output BR
);

  wire and_1_out;

  and and_1 (and_1_out, CBR, Z);
  or or_1 (BR, and_1_out, UBR);
endmodule
